// Logisim project Mir Faiyaz Hossain_2011385042_Lab_1.circ as structural Verilog
module _1_bit_LU (
  input  A1,
  input  B1,
  input  [1:0] S1S2,
  output F1
);

  wire and_1_out, not_1_out, or_1_out, xor_1_out;

  and and_1 (and_1_out, A1, B1);
  or or_1 (or_1_out, A1, B1);
  xor xor_1 (xor_1_out, A1, B1);
  not not_1 (not_1_out, A1);
  Multiplexer #(.select(2), .enable("false")) multiplexer_1 (
    .in0(and_1_out), .in1(or_1_out), .in2(xor_1_out), .in3(not_1_out), .out(F1), .sel(S1S2));
endmodule

module _2_bit_LU (
  input  A2,
  input  A1,
  input  B2,
  input  B1,
  input  [1:0] S1S2,
  output F2,
  output F1
);

  _1_bit_LU u_1_bit_lu_1 (.S1S2(S1S2), .F1(F1), .A1(A1), .B1(B1));
  _1_bit_LU u_1_bit_lu_2 (.S1S2(S1S2), .F1(F2), .A1(A2), .B1(B2));
endmodule

module LAB_MAIN_2_BIT_LU (
  input  A2,
  input  A1,
  input  B2,
  input  B1,
  input  [1:0] S1S2,
  output F2,
  output F1
);

  wire and_1_out, and_2_out, not_1_out, not_2_out, or_1_out, or_2_out, xor_1_out, xor_2_out;

  and and_1 (and_1_out, A1, B1);
  or or_1 (or_1_out, A1, B1);
  xor xor_1 (xor_1_out, A1, B1);
  not not_1 (not_1_out, A1);
  and and_2 (and_2_out, A2, B2);
  or or_2 (or_2_out, A2, B2);
  xor xor_2 (xor_2_out, A2, B2);
  not not_2 (not_2_out, A2);
  Multiplexer #(.select(2), .enable("false")) multiplexer_1 (
    .in0(and_1_out), .in1(or_1_out), .in2(xor_1_out), .in3(not_1_out), .out(F1), .sel(S1S2));
  Multiplexer #(.select(2), .enable("false")) multiplexer_2 (
    .in0(and_2_out), .in1(or_2_out), .in2(xor_2_out), .in3(not_2_out), .out(F2), .sel(S1S2));
endmodule

module _4_bit_LU (
  input  A4,
  input  A3,
  input  A2,
  input  A1,
  input  B4,
  input  B3,
  input  B2,
  input  B1,
  input  [1:0] S1S2,
  output F4,
  output F3,
  output F,
  output F1
);

  LAB_MAIN_2_BIT_LU lab_main_2_bit_lu_1 (.S1S2(S1S2), .A2(A2), .A1(A1), .B2(B2), .B1(B1), .F2(F), .F1(F1));
  LAB_MAIN_2_BIT_LU lab_main_2_bit_lu_2 (.S1S2(S1S2), .A2(A4), .A1(A3), .B2(B4), .B1(B3), .F2(F4), .F1(F3));
endmodule

module _8_bit_LU (
  input  A8,
  input  A7,
  input  A6,
  input  A5,
  input  A4,
  input  A3,
  input  A2,
  input  A1,
  input  B8,
  input  B7,
  input  B6,
  input  B5,
  input  B4,
  input  B3,
  input  B2,
  input  B1,
  input  [1:0] S1S2,
  output F8,
  output F7,
  output F6,
  output F5,
  output F4,
  output F3,
  output F2,
  output F1
);

  LAB_MAIN_2_BIT_LU lab_main_2_bit_lu_1 (.S1S2(S1S2), .A2(A8), .A1(A7), .B2(B8), .B1(B7), .F2(F8), .F1(F7));
  LAB_MAIN_2_BIT_LU lab_main_2_bit_lu_2 (.S1S2(S1S2), .A2(A6), .A1(A5), .B2(B6), .B1(B5), .F2(F6), .F1(F5));
  LAB_MAIN_2_BIT_LU lab_main_2_bit_lu_3 (.S1S2(S1S2), .A2(A4), .A1(A3), .B2(B4), .B1(B3), .F2(F4), .F1(F3));
  LAB_MAIN_2_BIT_LU lab_main_2_bit_lu_4 (.S1S2(S1S2), .A2(A2), .A1(A1), .B2(B2), .B1(B1), .F2(F2), .F1(F1));
endmodule

module _4_bit_ALU (
  input  [1:0] S1S0,
  input  Cin,
  input  A3,
  input  A2,
  input  A1,
  input  A0,
  input  B3,
  input  B2,
  input  B1,
  input  B0,
  output Cout,
  output D3,
  output D2,
  output D1,
  output D0
);

  wire adder_1_cout, adder_2_cout, adder_3_cout, multiplexer_1_out, multiplexer_2_out, multiplexer_3_out,
       multiplexer_4_out, not_1_out, not_2_out, not_3_out, not_4_out, not_5_out;

  not not_1 (not_1_out, 1'b0);
  not not_2 (not_2_out, B0);
  not not_3 (not_3_out, B1);
  not not_4 (not_4_out, B2);
  not not_5 (not_5_out, B3);
  Multiplexer #(.select(2), .enable("false")) multiplexer_1 (
    .in0(B0), .in1(not_2_out), .in2(1'b0), .in3(not_1_out), .out(multiplexer_1_out), .sel(S1S0));
  Multiplexer #(.select(2), .enable("false")) multiplexer_2 (
    .in0(B1), .in1(not_3_out), .in2(1'b0), .in3(not_1_out), .out(multiplexer_2_out), .sel(S1S0));
  Multiplexer #(.select(2), .enable("false")) multiplexer_3 (
    .in0(B2), .in1(not_4_out), .in2(1'b0), .in3(not_1_out), .out(multiplexer_3_out), .sel(S1S0));
  Multiplexer #(.select(2), .enable("false")) multiplexer_4 (
    .in0(B3), .in1(not_5_out), .in2(1'b0), .in3(not_1_out), .out(multiplexer_4_out), .sel(S1S0));
  Adder #(.width(1)) adder_1 (.a(A0), .b(multiplexer_1_out), .out(D0), .cin(Cin), .cout(adder_1_cout));
  Adder #(.width(1)) adder_2 (.a(A1), .b(multiplexer_2_out), .out(D1), .cin(adder_1_cout), .cout(adder_2_cout));
  Adder #(.width(1)) adder_3 (.a(A2), .b(multiplexer_3_out), .out(D2), .cin(adder_2_cout), .cout(adder_3_cout));
  Adder #(.width(1)) adder_4 (.a(A3), .b(multiplexer_4_out), .out(D3), .cin(adder_3_cout), .cout(Cout));

  // Notes on the sheet:
  //   1
  //   LAB 2
endmodule

module _8_bit_ALU (
  input  [1:0] S1S0,
  input  Cin,
  input  A7,
  input  A6,
  input  A5,
  input  A4,
  input  A3,
  input  A2,
  input  A1,
  input  A0,
  input  B7,
  input  B6,
  input  B5,
  input  B4,
  input  B3,
  input  B2,
  input  B1,
  input  B0,
  output Cout,
  output D7,
  output D6,
  output D5,
  output D4,
  output D3,
  output D2,
  output D1,
  output D0
);

  wire n4_bit_alu_2_cout;

  _4_bit_ALU u_4_bit_alu_1 (
    .S1S0(S1S0), .Cin(n4_bit_alu_2_cout), .A3(A7), .A2(A6), .A1(A5), .A0(A4), .B3(B7), .B2(B6), .B1(B5),
    .B0(B4), .Cout(Cout), .D3(D7), .D2(D6), .D1(D5), .D0(D4));
  _4_bit_ALU u_4_bit_alu_2 (
    .S1S0(S1S0), .Cin(Cin), .A3(A3), .A2(A2), .A1(A1), .A0(A0), .B3(B3), .B2(B2), .B1(B1), .B0(B0),
    .Cout(n4_bit_alu_2_cout), .D3(D3), .D2(D2), .D1(D1), .D0(D0));

  // Notes on the sheet:
  //   8-BIT ALU IMPLEMENTED USING 2x 4-BIT ALU
endmodule

module _4_bit_Multiplier (
  input  A4,
  input  A3,
  input  A2,
  input  A1,
  input  B4,
  input  B3,
  input  B2,
  input  B1,
  input  _0,
  output S8,
  output S7,
  output S6,
  output S5,
  output S4,
  output S3,
  output S2,
  output S1
);

  wire and_2_out, and_3_out, and_4_out, and_5_out, and_6_out, and_7_out, and_8_out, and_9_out, and_10_out,
       and_11_out, and_12_out, and_13_out, and_14_out, and_15_out, and_16_out, n4_bit_adder_1_cout,
       n4_bit_adder_1_s2, n4_bit_adder_1_s3, n4_bit_adder_1_s4, n4_bit_adder_2_cout, n4_bit_adder_2_s2,
       n4_bit_adder_2_s3, n4_bit_adder_2_s4;

  and and_1 (S1, B1, A1);
  and and_2 (and_2_out, B4, A1);
  and and_3 (and_3_out, B3, A1);
  and and_4 (and_4_out, B2, A1);
  and and_5 (and_5_out, B4, A2);
  and and_6 (and_6_out, B3, A2);
  and and_7 (and_7_out, B2, A2);
  and and_8 (and_8_out, B1, A2);
  and and_9 (and_9_out, B4, A3);
  and and_10 (and_10_out, B3, A3);
  and and_11 (and_11_out, B2, A3);
  and and_12 (and_12_out, B1, A3);
  and and_13 (and_13_out, B4, A4);
  and and_14 (and_14_out, B3, A4);
  and and_15 (and_15_out, B2, A4);
  and and_16 (and_16_out, B1, A4);
  _4_bit_ADDER u_4_bit_adder_1 (
    .A4(_0), .A3(and_2_out), .A2(and_3_out), .A1(and_4_out), .B4(and_5_out), .B3(and_6_out), .B2(and_7_out),
    .B1(and_8_out), .Cin(_0), .Cout(n4_bit_adder_1_cout), .S4(n4_bit_adder_1_s4), .S3(n4_bit_adder_1_s3),
    .S2(n4_bit_adder_1_s2), .S1(S2));
  _4_bit_ADDER u_4_bit_adder_2 (
    .A4(n4_bit_adder_1_cout), .A3(n4_bit_adder_1_s4), .A2(n4_bit_adder_1_s3), .A1(n4_bit_adder_1_s2),
    .B4(and_9_out), .B3(and_10_out), .B2(and_11_out), .B1(and_12_out), .Cin(_0), .Cout(n4_bit_adder_2_cout),
    .S4(n4_bit_adder_2_s4), .S3(n4_bit_adder_2_s3), .S2(n4_bit_adder_2_s2), .S1(S3));
  _4_bit_ADDER u_4_bit_adder_3 (
    .A4(n4_bit_adder_2_cout), .A3(n4_bit_adder_2_s4), .A2(n4_bit_adder_2_s3), .A1(n4_bit_adder_2_s2),
    .B4(and_13_out), .B3(and_14_out), .B2(and_15_out), .B1(and_16_out), .Cin(_0), .Cout(S8), .S4(S7),
    .S3(S6), .S2(S5), .S1(S4));
  // Probe on {S8, S7, S6, S5, S4, S3, S2, S1}

  // Notes on the sheet:
  //   Multiplicand
  //   Multiplier
  //   Product
endmodule

module _4_bit_ADDER (
  input  A4,
  input  A3,
  input  A2,
  input  A1,
  input  B4,
  input  B3,
  input  B2,
  input  B1,
  input  Cin,
  output Cout,
  output S4,
  output S3,
  output S2,
  output S1
);

  wire adder_1_cout, adder_2_cout, adder_3_cout;

  Adder #(.width(1)) adder_1 (.a(A1), .b(B1), .out(S1), .cin(Cin), .cout(adder_1_cout));
  Adder #(.width(1)) adder_2 (.a(A2), .b(B2), .out(S2), .cin(adder_1_cout), .cout(adder_2_cout));
  Adder #(.width(1)) adder_3 (.a(A3), .b(B3), .out(S3), .cin(adder_2_cout), .cout(adder_3_cout));
  Adder #(.width(1)) adder_4 (.a(A4), .b(B4), .out(S4), .cin(adder_3_cout), .cout(Cout));
endmodule

module _4_BIT_MULT_SUB_IMP (
  input  A4,
  input  A3,
  input  A2,
  input  A1,
  input  B4,
  input  B3,
  input  B2,
  input  B1,
  input  _0,
  output S8,
  output S7,
  output S6,
  output S5,
  output S4,
  output S3,
  output S2,
  output S1
);

  _4_bit_Multiplier u_4_bit_multiplier_1 (
    .A4(A4), .A3(A3), .A2(A2), .A1(A1), .B4(B4), .B3(B3), .B2(B2), .B1(B1), ._0(_0), .S8(S8), .S7(S7),
    .S6(S6), .S5(S5), .S4(S4), .S3(S3), .S2(S2), .S1(S1));
  // Probe on {S8, S7, S6, S5, S4, S3, S2, S1}

  // Notes on the sheet:
  //   Multiplicand
  //   Multiplier
  //   Product
endmodule

module _8x8_bit_Multiplier (
  input  A8,
  input  A7,
  input  A6,
  input  A5,
  input  A4,
  input  A3,
  input  A2,
  input  A1,
  input  B8,
  input  B7,
  input  B6,
  input  B5,
  input  B4,
  input  B3,
  input  B2,
  input  B1,
  input  _0,
  output S16,
  output S15,
  output S14,
  output S13,
  output S12,
  output S11,
  output S10,
  output S9,
  output S8,
  output S7,
  output S6,
  output S5,
  output S4,
  output S3,
  output S2,
  output S1
);

  wire and_1_out, and_2_out, and_3_out, and_4_out, and_5_out, and_6_out, and_7_out, and_8_out, and_9_out,
       and_10_out, and_11_out, and_12_out, and_13_out, and_14_out, and_15_out, and_16_out, and_17_out,
       and_18_out, and_19_out, and_20_out, and_21_out, and_22_out, and_23_out, and_24_out, and_26_out,
       and_27_out, and_28_out, and_29_out, and_30_out, and_31_out, and_32_out, and_33_out, and_34_out,
       and_35_out, and_36_out, and_37_out, and_38_out, and_39_out, and_40_out, and_41_out, and_42_out,
       and_43_out, and_44_out, and_45_out, and_46_out, and_47_out, and_48_out, and_49_out, and_50_out,
       and_51_out, and_52_out, and_53_out, and_54_out, and_55_out, and_56_out, and_57_out, and_58_out,
       and_59_out, and_60_out, and_61_out, and_62_out, and_63_out, and_64_out, n8_bit_adder_1_cout,
       n8_bit_adder_1_s2, n8_bit_adder_1_s3, n8_bit_adder_1_s4, n8_bit_adder_1_s5, n8_bit_adder_1_s6,
       n8_bit_adder_1_s7, n8_bit_adder_1_s8, n8_bit_adder_2_cout, n8_bit_adder_2_s2, n8_bit_adder_2_s3,
       n8_bit_adder_2_s4, n8_bit_adder_2_s5, n8_bit_adder_2_s6, n8_bit_adder_2_s7, n8_bit_adder_2_s8,
       n8_bit_adder_3_cout, n8_bit_adder_3_s2, n8_bit_adder_3_s3, n8_bit_adder_3_s4, n8_bit_adder_3_s5,
       n8_bit_adder_3_s6, n8_bit_adder_3_s7, n8_bit_adder_3_s8, n8_bit_adder_4_cout, n8_bit_adder_4_s2,
       n8_bit_adder_4_s3, n8_bit_adder_4_s4, n8_bit_adder_4_s5, n8_bit_adder_4_s6, n8_bit_adder_4_s7,
       n8_bit_adder_4_s8, n8_bit_adder_5_cout, n8_bit_adder_5_s2, n8_bit_adder_5_s3, n8_bit_adder_5_s4,
       n8_bit_adder_5_s5, n8_bit_adder_5_s6, n8_bit_adder_5_s7, n8_bit_adder_5_s8, n8_bit_adder_6_cout,
       n8_bit_adder_6_s2, n8_bit_adder_6_s3, n8_bit_adder_6_s4, n8_bit_adder_6_s5, n8_bit_adder_6_s6,
       n8_bit_adder_6_s7, n8_bit_adder_6_s8;

  and and_1 (and_1_out, B8, A6);
  and and_2 (and_2_out, B7, A6);
  and and_3 (and_3_out, B6, A6);
  and and_4 (and_4_out, B5, A6);
  and and_5 (and_5_out, B4, A6);
  and and_6 (and_6_out, B3, A6);
  and and_7 (and_7_out, B2, A6);
  and and_8 (and_8_out, B1, A6);
  and and_9 (and_9_out, B8, A7);
  and and_10 (and_10_out, B7, A7);
  and and_11 (and_11_out, B6, A7);
  and and_12 (and_12_out, B5, A7);
  and and_13 (and_13_out, B4, A7);
  and and_14 (and_14_out, B3, A7);
  and and_15 (and_15_out, B2, A7);
  and and_16 (and_16_out, B1, A7);
  and and_17 (and_17_out, B8, A8);
  and and_18 (and_18_out, B7, A8);
  and and_19 (and_19_out, B6, A8);
  and and_20 (and_20_out, B5, A8);
  and and_21 (and_21_out, B4, A8);
  and and_22 (and_22_out, B3, A8);
  and and_23 (and_23_out, B2, A8);
  and and_24 (and_24_out, B1, A8);
  and and_25 (S1, B1, A1);
  and and_26 (and_26_out, B8, A1);
  and and_27 (and_27_out, B7, A1);
  and and_28 (and_28_out, B6, A1);
  and and_29 (and_29_out, B5, A1);
  and and_30 (and_30_out, B4, A1);
  and and_31 (and_31_out, B3, A1);
  and and_32 (and_32_out, B2, A1);
  and and_33 (and_33_out, B8, A2);
  and and_34 (and_34_out, B7, A2);
  and and_35 (and_35_out, B6, A2);
  and and_36 (and_36_out, B5, A2);
  and and_37 (and_37_out, B4, A2);
  and and_38 (and_38_out, B3, A2);
  and and_39 (and_39_out, B2, A2);
  and and_40 (and_40_out, B1, A2);
  and and_41 (and_41_out, B8, A3);
  and and_42 (and_42_out, B7, A3);
  and and_43 (and_43_out, B6, A3);
  and and_44 (and_44_out, B5, A3);
  and and_45 (and_45_out, B4, A3);
  and and_46 (and_46_out, B3, A3);
  and and_47 (and_47_out, B2, A3);
  and and_48 (and_48_out, B1, A3);
  and and_49 (and_49_out, B8, A4);
  and and_50 (and_50_out, B7, A4);
  and and_51 (and_51_out, B6, A4);
  and and_52 (and_52_out, B5, A4);
  and and_53 (and_53_out, B4, A4);
  and and_54 (and_54_out, B3, A4);
  and and_55 (and_55_out, B2, A4);
  and and_56 (and_56_out, B1, A4);
  and and_57 (and_57_out, B8, A5);
  and and_58 (and_58_out, B7, A5);
  and and_59 (and_59_out, B6, A5);
  and and_60 (and_60_out, B5, A5);
  and and_61 (and_61_out, B4, A5);
  and and_62 (and_62_out, B3, A5);
  and and_63 (and_63_out, B2, A5);
  and and_64 (and_64_out, B1, A5);
  _8_bit_Adder u_8_bit_adder_1 (
    .Cin(_0), .A7(_0), .A6(and_26_out), .A5(and_27_out), .A4(and_28_out), .A3(and_29_out), .A2(and_30_out),
    .A1(and_31_out), .A0(and_32_out), .B7(and_33_out), .B6(and_34_out), .B5(and_35_out), .B4(and_36_out),
    .B3(and_37_out), .B2(and_38_out), .B1(and_39_out), .B0(and_40_out), .Cout(n8_bit_adder_1_cout),
    .S8(n8_bit_adder_1_s8), .S7(n8_bit_adder_1_s7), .S6(n8_bit_adder_1_s6), .S5(n8_bit_adder_1_s5),
    .S4(n8_bit_adder_1_s4), .S3(n8_bit_adder_1_s3), .S2(n8_bit_adder_1_s2), .S1(S2));
  _8_bit_Adder u_8_bit_adder_2 (
    .Cin(_0), .A7(n8_bit_adder_1_cout), .A6(n8_bit_adder_1_s8), .A5(n8_bit_adder_1_s7),
    .A4(n8_bit_adder_1_s6), .A3(n8_bit_adder_1_s5), .A2(n8_bit_adder_1_s4), .A1(n8_bit_adder_1_s3),
    .A0(n8_bit_adder_1_s2), .B7(and_41_out), .B6(and_42_out), .B5(and_43_out), .B4(and_44_out),
    .B3(and_45_out), .B2(and_46_out), .B1(and_47_out), .B0(and_48_out), .Cout(n8_bit_adder_2_cout),
    .S8(n8_bit_adder_2_s8), .S7(n8_bit_adder_2_s7), .S6(n8_bit_adder_2_s6), .S5(n8_bit_adder_2_s5),
    .S4(n8_bit_adder_2_s4), .S3(n8_bit_adder_2_s3), .S2(n8_bit_adder_2_s2), .S1(S3));
  _8_bit_Adder u_8_bit_adder_3 (
    .Cin(_0), .A7(n8_bit_adder_2_cout), .A6(n8_bit_adder_2_s8), .A5(n8_bit_adder_2_s7),
    .A4(n8_bit_adder_2_s6), .A3(n8_bit_adder_2_s5), .A2(n8_bit_adder_2_s4), .A1(n8_bit_adder_2_s3),
    .A0(n8_bit_adder_2_s2), .B7(and_49_out), .B6(and_50_out), .B5(and_51_out), .B4(and_52_out),
    .B3(and_53_out), .B2(and_54_out), .B1(and_55_out), .B0(and_56_out), .Cout(n8_bit_adder_3_cout),
    .S8(n8_bit_adder_3_s8), .S7(n8_bit_adder_3_s7), .S6(n8_bit_adder_3_s6), .S5(n8_bit_adder_3_s5),
    .S4(n8_bit_adder_3_s4), .S3(n8_bit_adder_3_s3), .S2(n8_bit_adder_3_s2), .S1(S4));
  _8_bit_Adder u_8_bit_adder_4 (
    .Cin(_0), .A7(n8_bit_adder_3_cout), .A6(n8_bit_adder_3_s8), .A5(n8_bit_adder_3_s7),
    .A4(n8_bit_adder_3_s6), .A3(n8_bit_adder_3_s5), .A2(n8_bit_adder_3_s4), .A1(n8_bit_adder_3_s3),
    .A0(n8_bit_adder_3_s2), .B7(and_57_out), .B6(and_58_out), .B5(and_59_out), .B4(and_60_out),
    .B3(and_61_out), .B2(and_62_out), .B1(and_63_out), .B0(and_64_out), .Cout(n8_bit_adder_4_cout),
    .S8(n8_bit_adder_4_s8), .S7(n8_bit_adder_4_s7), .S6(n8_bit_adder_4_s6), .S5(n8_bit_adder_4_s5),
    .S4(n8_bit_adder_4_s4), .S3(n8_bit_adder_4_s3), .S2(n8_bit_adder_4_s2), .S1(S5));
  _8_bit_Adder u_8_bit_adder_5 (
    .Cin(_0), .A7(n8_bit_adder_4_cout), .A6(n8_bit_adder_4_s8), .A5(n8_bit_adder_4_s7),
    .A4(n8_bit_adder_4_s6), .A3(n8_bit_adder_4_s5), .A2(n8_bit_adder_4_s4), .A1(n8_bit_adder_4_s3),
    .A0(n8_bit_adder_4_s2), .B7(and_1_out), .B6(and_2_out), .B5(and_3_out), .B4(and_4_out), .B3(and_5_out),
    .B2(and_6_out), .B1(and_7_out), .B0(and_8_out), .Cout(n8_bit_adder_5_cout), .S8(n8_bit_adder_5_s8),
    .S7(n8_bit_adder_5_s7), .S6(n8_bit_adder_5_s6), .S5(n8_bit_adder_5_s5), .S4(n8_bit_adder_5_s4),
    .S3(n8_bit_adder_5_s3), .S2(n8_bit_adder_5_s2), .S1(S6));
  _8_bit_Adder u_8_bit_adder_6 (
    .Cin(_0), .A7(n8_bit_adder_5_cout), .A6(n8_bit_adder_5_s8), .A5(n8_bit_adder_5_s7),
    .A4(n8_bit_adder_5_s6), .A3(n8_bit_adder_5_s5), .A2(n8_bit_adder_5_s4), .A1(n8_bit_adder_5_s3),
    .A0(n8_bit_adder_5_s2), .B7(and_9_out), .B6(and_10_out), .B5(and_11_out), .B4(and_12_out),
    .B3(and_13_out), .B2(and_14_out), .B1(and_15_out), .B0(and_16_out), .Cout(n8_bit_adder_6_cout),
    .S8(n8_bit_adder_6_s8), .S7(n8_bit_adder_6_s7), .S6(n8_bit_adder_6_s6), .S5(n8_bit_adder_6_s5),
    .S4(n8_bit_adder_6_s4), .S3(n8_bit_adder_6_s3), .S2(n8_bit_adder_6_s2), .S1(S7));
  _8_bit_Adder u_8_bit_adder_7 (
    .Cin(_0), .A7(n8_bit_adder_6_cout), .A6(n8_bit_adder_6_s8), .A5(n8_bit_adder_6_s7),
    .A4(n8_bit_adder_6_s6), .A3(n8_bit_adder_6_s5), .A2(n8_bit_adder_6_s4), .A1(n8_bit_adder_6_s3),
    .A0(n8_bit_adder_6_s2), .B7(and_17_out), .B6(and_18_out), .B5(and_19_out), .B4(and_20_out),
    .B3(and_21_out), .B2(and_22_out), .B1(and_23_out), .B0(and_24_out), .Cout(S16), .S8(S15), .S7(S14),
    .S6(S13), .S5(S12), .S4(S11), .S3(S10), .S2(S9), .S1(S8));
  // Probe on {S16, S15, S14, S13, S12, S11, S10, S9, S8, S7, S6, S5, S4, S3, S2, S1}
endmodule

module _8_bit_Adder (
  input  Cin,
  input  A7,
  input  A6,
  input  A5,
  input  A4,
  input  A3,
  input  A2,
  input  A1,
  input  A0,
  input  B7,
  input  B6,
  input  B5,
  input  B4,
  input  B3,
  input  B2,
  input  B1,
  input  B0,
  output Cout,
  output S8,
  output S7,
  output S6,
  output S5,
  output S4,
  output S3,
  output S2,
  output S1
);

  wire adder_1_cout, adder_2_cout, adder_3_cout, adder_4_cout, adder_5_cout, adder_6_cout, adder_7_cout;

  Adder #(.width(1)) adder_1 (.a(B0), .b(A0), .out(S1), .cin(Cin), .cout(adder_1_cout));
  Adder #(.width(1)) adder_2 (.a(A1), .b(B1), .out(S2), .cin(adder_1_cout), .cout(adder_2_cout));
  Adder #(.width(1)) adder_3 (.a(A2), .b(B2), .out(S3), .cin(adder_2_cout), .cout(adder_3_cout));
  Adder #(.width(1)) adder_4 (.a(A3), .b(B3), .out(S4), .cin(adder_3_cout), .cout(adder_4_cout));
  Adder #(.width(1)) adder_5 (.a(A4), .b(B4), .out(S5), .cin(adder_4_cout), .cout(adder_5_cout));
  Adder #(.width(1)) adder_6 (.a(A5), .b(B5), .out(S6), .cin(adder_5_cout), .cout(adder_6_cout));
  Adder #(.width(1)) adder_7 (.a(A6), .b(B6), .out(S7), .cin(adder_6_cout), .cout(adder_7_cout));
  Adder #(.width(1)) adder_8 (.a(A7), .b(B7), .out(S8), .cin(adder_7_cout), .cout(Cout));
endmodule

module _8x8_MULT_SUB_IMP (
  input  A8,
  input  A7,
  input  A6,
  input  A5,
  input  A4,
  input  A3,
  input  A2,
  input  A1,
  input  B8,
  input  B7,
  input  B6,
  input  B5,
  input  B4,
  input  B3,
  input  B2,
  input  B1,
  input  _0,
  output S16,
  output S15,
  output S14,
  output S13,
  output S12,
  output S11,
  output S10,
  output S9,
  output S8,
  output S7,
  output S6,
  output S5,
  output S4,
  output S3,
  output S2,
  output S1
);

  _8x8_bit_Multiplier u_8x8_bit_multiplier_1 (
    .A8(A8), .A7(A7), .A6(A6), .A5(A5), .A4(A4), .A3(A3), .A2(A2), .A1(A1), .B8(B8), .B7(B7), .B6(B6),
    .B5(B5), .B4(B4), .B3(B3), .B2(B2), .B1(B1), ._0(_0), .S16(S16), .S15(S15), .S14(S14), .S13(S13),
    .S12(S12), .S11(S11), .S10(S10), .S9(S9), .S8(S8), .S7(S7), .S6(S6), .S5(S5), .S4(S4), .S3(S3), .S2(S2),
    .S1(S1));
  // Probe on {S16, S15, S14, S13, S12, S11, S10, S9, S8, S7, S6, S5, S4, S3, S2, S1}
endmodule

module _1_bit_ALU_lab4 (
  input  Cin,
  input  a,
  input  b,
  input  [2:0] Operation,
  input  Binvert,
  output Result,
  output Cin_2
);

  wire adder_1_out, and_1_out, comparator_1_lt, multiplexer_1_out, not_1_out, or_1_out;

  Multiplexer #(.enable("false")) multiplexer_1 (.in0(b), .in1(not_1_out), .out(multiplexer_1_out), .sel(Binvert));
  not not_1 (not_1_out, b);
  and and_1 (and_1_out, a, multiplexer_1_out);
  or or_1 (or_1_out, a, multiplexer_1_out);
  Adder #(.width(1)) adder_1 (.a(a), .b(multiplexer_1_out), .out(adder_1_out), .cin(Cin), .cout(Cin_2));
  Comparator #(.width(1), .mode("unsigned")) comparator_1 (.a(a), .b(b), .lt(comparator_1_lt));  // open: gt, eq
  Multiplexer #(.select(3), .enable("false")) multiplexer_2 (
    .in0(and_1_out), .in1(or_1_out), .in2(adder_1_out), .in3(1'b0), .in4(1'b0), .in5(1'b0),
    .in6(adder_1_out), .in7(comparator_1_lt), .out(Result), .sel(Operation));
endmodule

module _4_bit_ALU_lab4 (
  input  Cin,
  input  [2:0] Operation,
  input  Binvert,
  input  A0,
  input  B0,
  input  A1,
  input  B1,
  input  A2,
  input  B2,
  input  A3,
  input  B3,
  output Result0,
  output Result1,
  output Result2,
  output Result3,
  output Cout
);

  wire n1_bit_alu_lab4_1_cin_2, n1_bit_alu_lab4_2_cin_2, n1_bit_alu_lab4_3_cin_2;

  _1_bit_ALU_lab4 u_1_bit_alu_lab4_1 (
    .a(A0), .b(B0), .Cin(Cin), .Binvert(Binvert), .Operation(Operation), .Cin_2(n1_bit_alu_lab4_1_cin_2),
    .Result(Result0));
  _1_bit_ALU_lab4 u_1_bit_alu_lab4_2 (
    .a(A1), .b(B1), .Cin(n1_bit_alu_lab4_1_cin_2), .Binvert(Binvert), .Operation(Operation),
    .Cin_2(n1_bit_alu_lab4_2_cin_2), .Result(Result1));
  _1_bit_ALU_lab4 u_1_bit_alu_lab4_3 (
    .a(A2), .b(B2), .Cin(n1_bit_alu_lab4_2_cin_2), .Binvert(Binvert), .Operation(Operation),
    .Cin_2(n1_bit_alu_lab4_3_cin_2), .Result(Result2));
  _1_bit_ALU_lab4 u_1_bit_alu_lab4_4 (
    .a(A3), .b(B3), .Cin(n1_bit_alu_lab4_3_cin_2), .Binvert(Binvert), .Operation(Operation), .Cin_2(Cout),
    .Result(Result3));
endmodule

// ALUop
module ALU_Control_lab_4 (
  input  [1:0] ALUop,
  input  [5:0] F_5_0,
  output [2:0] ALUop_2
);

  wire and_1_out, not_1_out, not_2_out, or_1_out;

  or or_1 (or_1_out, F_5_0[3], F_5_0[0]);
  and and_1 (and_1_out, ALUop[1], F_5_0[1]);
  and and_2 (ALUop_2[0], ALUop[1], or_1_out);
  not not_1 (not_1_out, ALUop[1]);
  not not_2 (not_2_out, F_5_0[2]);
  or or_2 (ALUop_2[2], ALUop[0], and_1_out);
  or or_3 (ALUop_2[1], not_1_out, not_2_out);

  // Notes on the sheet:
  //   Op0
  //   Op2
  //   Op1
endmodule

module Lab_4_ALU_with_control (
  input  Binvert,
  input  Cin,
  input  A4,
  input  A3,
  input  A2,
  input  A1,
  input  B4,
  input  B3,
  input  B2,
  input  B1,
  input  [1:0] ALUop,
  input  [5:0] F_5_0,
  output Result3,
  output Result2,
  output Result1,
  output Result0,
  output Cout
);

  wire [2:0] alu_control_lab_4_1_aluop_2;

  _4_bit_ALU_lab4 u_4_bit_alu_lab4_1 (
    .A0(A1), .B0(B1), .A1(A2), .B1(B2), .A2(A3), .B2(B3), .A3(A4), .B3(B4), .Result0(Result0),
    .Result1(Result1), .Result2(Result2), .Result3(Result3), .Binvert(Binvert), .Cin(Cin),
    .Operation(alu_control_lab_4_1_aluop_2), .Cout(Cout));
  ALU_Control_lab_4 alu_control_lab_4_1 (.ALUop_2(alu_control_lab_4_1_aluop_2), .F_5_0(F_5_0), .ALUop(ALUop));
endmodule

module MID_TASK_1 (
  input  A3,
  input  A2,
  input  A1,
  input  B3,
  input  B2,
  input  B1,
  input  _0,
  output S6,
  output S5,
  output S4,
  output S3,
  output S2,
  output S1
);

  wire and_2_out, and_3_out, and_4_out, and_5_out, and_6_out, and_7_out, and_8_out, and_9_out,
       n4_bit_adder_1_cout, n4_bit_adder_1_s2, n4_bit_adder_1_s3;

  and and_1 (S1, B1, A1);
  and and_2 (and_2_out, B3, A1);
  and and_3 (and_3_out, B2, A1);
  and and_4 (and_4_out, B3, A2);
  and and_5 (and_5_out, B2, A2);
  and and_6 (and_6_out, B1, A2);
  and and_7 (and_7_out, B3, A3);
  and and_8 (and_8_out, B2, A3);
  and and_9 (and_9_out, B1, A3);
  _4_bit_ADDER u_4_bit_adder_1 (
    .A4(_0), .A3(_0), .A2(and_2_out), .A1(and_3_out), .B4(_0), .B3(and_4_out), .B2(and_5_out),
    .B1(and_6_out), .Cin(_0), .Cout(n4_bit_adder_1_cout), .S3(n4_bit_adder_1_s3), .S2(n4_bit_adder_1_s2),
    .S1(S2));  // open: S4
  _4_bit_ADDER u_4_bit_adder_2 (
    .A4(_0), .A3(n4_bit_adder_1_cout), .A2(n4_bit_adder_1_s3), .A1(n4_bit_adder_1_s2), .B4(_0),
    .B3(and_7_out), .B2(and_8_out), .B1(and_9_out), .Cin(_0), .Cout(S6), .S3(S5), .S2(S4), .S1(S3));  // open: S4
  // Probe on {S6, S5, S4, S3, S2, S1}

  // Notes on the sheet:
  //   Multiplicand
  //   Multiplier
  //   Product
endmodule

module MID_TASK_2 (
  input  Cin,
  input  a,
  input  [2:0] Operation,
  input  b,
  output Result,
  output Cin_2
);

  wire adder_1_out, and_1_out, nand_1_out, nor_1_out, not_1_out, or_1_out, xor_1_out;

  xor xor_1 (xor_1_out, a, b);
  not not_1 (not_1_out, a);
  nand nand_1 (nand_1_out, b, a);
  nor nor_1 (nor_1_out, b, a);
  Adder #(.width(1)) adder_1 (.a(b), .b(a), .out(adder_1_out), .cin(Cin), .cout(Cin_2));
  or or_1 (or_1_out, b, a);
  and and_1 (and_1_out, a, b);
  Multiplexer #(.select(3), .enable("false")) multiplexer_1 (
    .in0(xor_1_out), .in1(not_1_out), .in2(nand_1_out), .in3(nor_1_out), .in4(adder_1_out), .in5(or_1_out),
    .in6(and_1_out), .in7(1'b0), .out(Result), .sel(Operation));
endmodule

module MID_TASK_2_Cascaded (
  input  [2:0] Operation,
  input  Cin,
  input  A0,
  input  B0,
  input  A1,
  input  B1,
  input  A2,
  input  B2,
  input  A3,
  input  B3,
  output Result0,
  output Result1,
  output Result2,
  output Result3,
  output Cout
);

  wire mid_task_2_1_cin_2, mid_task_2_2_cin_2, mid_task_2_3_cin_2;

  MID_TASK_2 mid_task_2_1 (
    .a(A0), .b(B0), .Result(Result0), .Cin_2(mid_task_2_1_cin_2), .Cin(Cin), .Operation(Operation));
  MID_TASK_2 mid_task_2_2 (
    .a(A1), .b(B1), .Result(Result1), .Cin_2(mid_task_2_2_cin_2), .Cin(mid_task_2_1_cin_2),
    .Operation(Operation));
  MID_TASK_2 mid_task_2_3 (
    .a(A2), .b(B2), .Result(Result2), .Cin_2(mid_task_2_3_cin_2), .Cin(mid_task_2_2_cin_2),
    .Operation(Operation));
  MID_TASK_2 mid_task_2_4 (
    .a(A3), .b(B3), .Result(Result3), .Cin_2(Cout), .Cin(mid_task_2_3_cin_2), .Operation(Operation));
endmodule

module Pre_Project_Task__4 (
  input  [1:0] ALUop,
  input  [5:0] F_5_0,
  input  Cin,
  input  A7,
  input  A6,
  input  A5,
  input  A4,
  input  A3,
  input  A2,
  input  A1,
  input  A0,
  input  B7,
  input  B6,
  input  B5,
  input  B4,
  input  B3,
  input  B2,
  input  B1,
  input  B0,
  input  Binvert,
  output Cout,
  output D7,
  output D6,
  output D5,
  output D4,
  output D3,
  output D2,
  output D1,
  output D0
);

  wire n4_bit_alu_lab4_1_cout;
  wire [2:0] alu_control_lab_4_1_aluop_2;

  ALU_Control_lab_4 alu_control_lab_4_1 (.ALUop_2(alu_control_lab_4_1_aluop_2), .F_5_0(F_5_0), .ALUop(ALUop));
  _4_bit_ALU_lab4 u_4_bit_alu_lab4_1 (
    .A0(A0), .B0(B0), .A1(A1), .B1(B1), .A2(A2), .B2(B2), .A3(A3), .B3(B3), .Result0(D0), .Result1(D1),
    .Result2(D2), .Result3(D3), .Binvert(Binvert), .Cin(Cin), .Operation(alu_control_lab_4_1_aluop_2),
    .Cout(n4_bit_alu_lab4_1_cout));
  _4_bit_ALU_lab4 u_4_bit_alu_lab4_2 (
    .A0(A4), .B0(B4), .A1(A5), .B1(B5), .A2(A6), .B2(B6), .A3(A7), .B3(B7), .Result0(D4), .Result1(D5),
    .Result2(D6), .Result3(D7), .Binvert(Binvert), .Cin(n4_bit_alu_lab4_1_cout),
    .Operation(alu_control_lab_4_1_aluop_2), .Cout(Cout));
endmodule

module _16_bit_ALU_LAB_5 (
  input  Binvert,
  input  Cin,
  input  [2:0] Operation,
  input  [15:0] A,
  input  [15:0] A_2,
  output [15:0] Result,
  output Cout
);

  wire n4_bit_alu_lab4_1_cout, n4_bit_alu_lab4_2_cout, n4_bit_alu_lab4_3_cout;

  _4_bit_ALU_lab4 u_4_bit_alu_lab4_1 (
    .A0(A[0]), .B0(A_2[0]), .A1(A[1]), .B1(A_2[1]), .A2(A[2]), .B2(A_2[2]), .A3(A[3]), .B3(A_2[3]),
    .Result0(Result[0]), .Result1(Result[1]), .Result2(Result[2]), .Result3(Result[3]), .Binvert(Binvert),
    .Cin(Cin), .Operation(Operation), .Cout(n4_bit_alu_lab4_1_cout));
  _4_bit_ALU_lab4 u_4_bit_alu_lab4_2 (
    .A0(A[4]), .B0(A_2[4]), .A1(A[5]), .B1(A_2[5]), .A2(A[6]), .B2(A_2[6]), .A3(A[7]), .B3(A_2[7]),
    .Result0(Result[4]), .Result1(Result[5]), .Result2(Result[6]), .Result3(Result[7]), .Binvert(Binvert),
    .Cin(n4_bit_alu_lab4_1_cout), .Operation(Operation), .Cout(n4_bit_alu_lab4_2_cout));
  _4_bit_ALU_lab4 u_4_bit_alu_lab4_3 (
    .A0(A[8]), .B0(A_2[8]), .A1(A[9]), .B1(A_2[9]), .A2(A[10]), .B2(A_2[10]), .A3(A[11]), .B3(A_2[11]),
    .Result0(Result[8]), .Result1(Result[9]), .Result2(Result[10]), .Result3(Result[11]), .Binvert(Binvert),
    .Cin(n4_bit_alu_lab4_2_cout), .Operation(Operation), .Cout(n4_bit_alu_lab4_3_cout));
  _4_bit_ALU_lab4 u_4_bit_alu_lab4_4 (
    .A0(A[12]), .B0(A_2[12]), .A1(A[13]), .B1(A_2[13]), .A2(A[14]), .B2(A_2[14]), .A3(A[15]), .B3(A_2[15]),
    .Result0(Result[12]), .Result1(Result[13]), .Result2(Result[14]), .Result3(Result[15]),
    .Binvert(Binvert), .Cin(n4_bit_alu_lab4_3_cout), .Operation(Operation), .Cout(Cout));
endmodule

module Register_File_LAB_5 (
  input  [15:0] Write,
  input  [3:0] RS,
  input  [3:0] RD,
  input  [3:0] RT,
  input  Wr_enable,
  input  Clock,
  output [15:0] Read_1,
  output [15:0] Read_2
);

  wire and_1_out, and_2_out, and_3_out, and_4_out, and_5_out, and_6_out, and_7_out, and_8_out, and_9_out,
       and_10_out, and_11_out, and_12_out, and_13_out, and_14_out, and_15_out, and_16_out, decoder_1_out0,
       decoder_1_out1, decoder_1_out2, decoder_1_out3, decoder_1_out4, decoder_1_out5, decoder_1_out6,
       decoder_1_out7, decoder_1_out8, decoder_1_out9, decoder_1_out10, decoder_1_out11, decoder_1_out12,
       decoder_1_out13, decoder_1_out14, decoder_1_out15;
  wire [15:0] R0_q, R1_q, R2_q, R3_q, R4_q, R5_q, R6_q, R7_q, R8_q, R9_q, R10_q, R11_q, R12_q, R13_q, R14_q,
       R15_q;

  Decoder #(.select(4), .enable("false")) decoder_1 (
    .out0(decoder_1_out0), .out1(decoder_1_out1), .out2(decoder_1_out2), .out3(decoder_1_out3),
    .out4(decoder_1_out4), .out5(decoder_1_out5), .out6(decoder_1_out6), .out7(decoder_1_out7),
    .out8(decoder_1_out8), .out9(decoder_1_out9), .out10(decoder_1_out10), .out11(decoder_1_out11),
    .out12(decoder_1_out12), .out13(decoder_1_out13), .out14(decoder_1_out14), .out15(decoder_1_out15),
    .sel(RD));
  and and_1 (and_1_out, decoder_1_out0, Wr_enable);
  and and_2 (and_2_out, decoder_1_out1, Wr_enable);
  and and_3 (and_3_out, decoder_1_out2, Wr_enable);
  and and_4 (and_4_out, decoder_1_out3, Wr_enable);
  and and_5 (and_5_out, decoder_1_out4, Wr_enable);
  and and_6 (and_6_out, decoder_1_out5, Wr_enable);
  and and_7 (and_7_out, decoder_1_out6, Wr_enable);
  and and_8 (and_8_out, decoder_1_out7, Wr_enable);
  and and_9 (and_9_out, decoder_1_out8, Wr_enable);
  and and_10 (and_10_out, decoder_1_out9, Wr_enable);
  and and_11 (and_11_out, decoder_1_out10, Wr_enable);
  and and_12 (and_12_out, decoder_1_out11, Wr_enable);
  and and_13 (and_13_out, decoder_1_out12, Wr_enable);
  and and_14 (and_14_out, decoder_1_out13, Wr_enable);
  and and_15 (and_15_out, decoder_1_out14, Wr_enable);
  and and_16 (and_16_out, decoder_1_out15, Wr_enable);
  Register #(.width(16)) R0 (.D(Write), .en(and_1_out), .Q(R0_q), .clk(Clock));  // open: clr
  Register #(.width(16)) R1 (.D(Write), .en(and_2_out), .Q(R1_q), .clk(Clock));  // open: clr
  Register #(.width(16)) R2 (.D(Write), .en(and_3_out), .Q(R2_q), .clk(Clock));  // open: clr
  Register #(.width(16)) R3 (.D(Write), .en(and_4_out), .Q(R3_q), .clk(Clock));  // open: clr
  Register #(.width(16)) R4 (.D(Write), .en(and_5_out), .Q(R4_q), .clk(Clock));  // open: clr
  Register #(.width(16)) R5 (.D(Write), .en(and_6_out), .Q(R5_q), .clk(Clock));  // open: clr
  Register #(.width(16)) R6 (.D(Write), .en(and_7_out), .Q(R6_q), .clk(Clock));  // open: clr
  Register #(.width(16)) R7 (.D(Write), .en(and_8_out), .Q(R7_q), .clk(Clock));  // open: clr
  Register #(.width(16)) R8 (.D(Write), .en(and_9_out), .Q(R8_q), .clk(Clock));  // open: clr
  Register #(.width(16)) R9 (.D(Write), .en(and_10_out), .Q(R9_q), .clk(Clock));  // open: clr
  Register #(.width(16)) R10 (.D(Write), .en(and_11_out), .Q(R10_q), .clk(Clock));  // open: clr
  Register #(.width(16)) R11 (.D(Write), .en(and_12_out), .Q(R11_q), .clk(Clock));  // open: clr
  Register #(.width(16)) R12 (.D(Write), .en(and_13_out), .Q(R12_q), .clk(Clock));  // open: clr
  Register #(.width(16)) R13 (.D(Write), .en(and_14_out), .Q(R13_q), .clk(Clock));  // open: clr
  Register #(.width(16)) R14 (.D(Write), .en(and_15_out), .Q(R14_q), .clk(Clock));  // open: clr
  Register #(.width(16)) R15 (.D(Write), .en(and_16_out), .Q(R15_q), .clk(Clock));  // open: clr
  Multiplexer #(.select(4), .width(16), .enable("false")) multiplexer_1 (
    .in0(R0_q), .in1(R1_q), .in2(R2_q), .in3(R3_q), .in4(R4_q), .in5(R5_q), .in6(R6_q), .in7(R7_q),
    .in8(R8_q), .in9(R9_q), .in10(R10_q), .in11(R11_q), .in12(R12_q), .in13(R13_q), .in14(R14_q),
    .in15(R15_q), .out(Read_1), .sel(RS));
  Multiplexer #(.select(4), .width(16), .enable("false")) multiplexer_2 (
    .in0(R0_q), .in1(R1_q), .in2(R2_q), .in3(R3_q), .in4(R4_q), .in5(R5_q), .in6(R6_q), .in7(R7_q),
    .in8(R8_q), .in9(R9_q), .in10(R10_q), .in11(R11_q), .in12(R12_q), .in13(R13_q), .in14(R14_q),
    .in15(R15_q), .out(Read_2), .sel(RT));
endmodule

module R_Type_datapath (
  input  Binvert,
  input  Cin,
  input  [2:0] Operation,
  input  [3:0] RS,
  input  [3:0] RT,
  input  [3:0] RD,
  input  in_7,
  input  in_8,
  output [15:0] out_9,
  output out_10
);

  wire [15:0] register_file_lab_5_1_read_1, register_file_lab_5_1_read_2;

  Register_File_LAB_5 register_file_lab_5_1 (
    .Write(out_9), .Clock(in_7), .Read_1(register_file_lab_5_1_read_1),
    .Read_2(register_file_lab_5_1_read_2), .RD(RD), .Wr_enable(in_8), .RS(RS), .RT(RT));
  _16_bit_ALU_LAB_5 u_16_bit_alu_lab_5_1 (
    .A(register_file_lab_5_1_read_1), .A_2(register_file_lab_5_1_read_2), .Binvert(Binvert), .Cin(Cin),
    .Operation(Operation), .Cout(out_10), .Result(out_9));
endmodule

module Lab_6_R_type (
  input  Binvert,
  input  Cin,
  input  [2:0] Operation,
  input  in_4,
  output [3:0] Opcode,
  output [3:0] RS,
  output [3:0] RT,
  output [3:0] RD,
  output [15:0] out_9,
  output out_10
);

  wire button_1_out;
  wire [15:0] adder_1_out, register_1_q, register_file_lab_5_1_read_1, register_file_lab_5_1_read_2;

  Register #(.width(16)) register_1 (.D(adder_1_out), .Q(register_1_q), .clk(button_1_out));  // open: en, clr
  Adder #(.width(16)) adder_1 (.a(register_1_q), .b(16'h1), .out(adder_1_out));  // open: cin, cout
  ROM #(.addrWidth(16), .dataWidth(16)) rom_1 (.addr(register_1_q), .data({Opcode, RS, RT, RD}));  // open: sel
  Register_File_LAB_5 register_file_lab_5_1 (
    .Write(out_9), .Clock(button_1_out), .Read_1(register_file_lab_5_1_read_1),
    .Read_2(register_file_lab_5_1_read_2), .RD(RD), .Wr_enable(in_4), .RS(RS), .RT(RT));
  Button button_1 (.out(button_1_out));
  _16_bit_ALU_LAB_5 u_16_bit_alu_lab_5_1 (
    .A(register_file_lab_5_1_read_1), .A_2(register_file_lab_5_1_read_2), .Binvert(Binvert), .Cin(Cin),
    .Operation(Operation), .Cout(out_10), .Result(out_9));

  // Notes on the sheet:
  //   Add R2,R3,R6
  //   0000 0010 0011 0110
  //   0 2 3 6
  //   contents of rom_1 (hex, n*v repeats v):
  //   236 1547
  //   0001 0100 0101 0111
  //   1457
  //   Sub R4. R5. R7
endmodule

module Lab_6_I_type (
  input  Binvert,
  input  Cin,
  input  [2:0] Operation,
  input  in_4,
  output [3:0] Opcode,
  output [3:0] RS,
  output [3:0] RT,
  output [3:0] RD_IMM,
  output [15:0] out_9,
  output out_10
);

  wire button_1_out;
  wire [3:0] rom_1_data;
  wire [15:0] adder_1_out, bit_extender_1_out, register_1_q, register_file_lab_5_1_read_1;

  Register #(.width(16)) register_1 (.D(adder_1_out), .Q(register_1_q), .clk(button_1_out));  // open: en, clr
  Adder #(.width(16)) adder_1 (.a(register_1_q), .b(16'h1), .out(adder_1_out));  // open: cin, cout
  ROM #(.addrWidth(16), .dataWidth(16)) rom_1 (
    .addr(register_1_q), .data({Opcode, RS, RD_IMM, rom_1_data}));  // open: sel
  assign bit_extender_1_out = {{12{1'b0}}, rom_1_data};  // Bit_Extender bit_extender_1
  Register_File_LAB_5 register_file_lab_5_1 (
    .Write(out_9), .Clock(button_1_out), .Read_1(register_file_lab_5_1_read_1), .RD(RD_IMM),
    .Wr_enable(in_4), .RS(RS));  // open: Read_2, RT
  Button button_1 (.out(button_1_out));
  _16_bit_ALU_LAB_5 u_16_bit_alu_lab_5_1 (
    .A(register_file_lab_5_1_read_1), .A_2(bit_extender_1_out), .Binvert(Binvert), .Cin(Cin),
    .Operation(Operation), .Cout(out_10), .Result(out_9));

  assign RT = RD_IMM;

  // Notes on the sheet:
  //   0315
  //   addi, R3, R1, 5
  //   0000 0011 0001 0101
  //   contents of rom_1 (hex, n*v repeats v):
  //   315
endmodule

module Lab_7_Load_Store (
  input  Binvert,
  input  Cin,
  input  [2:0] Operation,
  input  in_4,
  input  store,
  input  load,
  output [3:0] Opcode,
  output [3:0] RS,
  output [3:0] RT,
  output [3:0] RD_IMM,
  output [15:0] out_11,
  output out_12
);

  wire button_1_out;
  wire [15:0] adder_1_out, bit_extender_1_out, ram_1_data, register_1_q, register_file_lab_5_1_read_1,
       register_file_lab_5_1_read_2;

  Register #(.width(16)) register_1 (.D(adder_1_out), .Q(register_1_q), .clk(button_1_out));  // open: en, clr
  Adder #(.width(16)) adder_1 (.a(register_1_q), .b(16'h1), .out(adder_1_out));  // open: cin, cout
  ROM #(.addrWidth(16), .dataWidth(16)) rom_1 (.addr(register_1_q), .data({Opcode, RS, RT, RD_IMM}));  // open: sel
  assign bit_extender_1_out = {{12{1'b0}}, RD_IMM};  // Bit_Extender bit_extender_1
  Register_File_LAB_5 register_file_lab_5_1 (
    .Write(ram_1_data), .Clock(button_1_out), .Read_1(register_file_lab_5_1_read_1),
    .Read_2(register_file_lab_5_1_read_2), .RD(RT), .Wr_enable(in_4), .RS(RS), .RT(RT));
  Button button_1 (.out(button_1_out));
  _16_bit_ALU_LAB_5 u_16_bit_alu_lab_5_1 (
    .A(register_file_lab_5_1_read_1), .A_2(bit_extender_1_out), .Binvert(Binvert), .Cin(Cin),
    .Operation(Operation), .Cout(out_12), .Result(out_11));
  RAM #(.addrWidth(16), .dataWidth(16), .bus("separate")) ram_1 (
    .addr(out_11), .din(register_file_lab_5_1_read_2), .data(ram_1_data), .str(store), .clk(button_1_out),
    .ld(load));  // open: sel, clr

  // Notes on the sheet:
  //   contents of rom_1 (hex, n*v repeats v):
  //   215
endmodule

module lab_7_Single_Cycle (
  input  Binvert,
  input  Cin,
  input  [2:0] Operation,
  input  in_4,
  input  in_5,
  input  in_6,
  input  store,
  input  load,
  input  in_9,
  output [3:0] Opcode,
  output [3:0] RS,
  output [3:0] RT,
  output [3:0] RD_IMM,
  output [15:0] out_14,
  output out_15
);

  wire button_1_out;
  wire [3:0] multiplexer_1_out;
  wire [15:0] adder_1_out, bit_extender_1_out, multiplexer_2_out, multiplexer_3_out, ram_1_data,
       register_1_q, register_file_lab_5_1_read_1, register_file_lab_5_1_read_2;

  Register #(.width(16)) register_1 (.D(adder_1_out), .Q(register_1_q), .clk(button_1_out));  // open: en, clr
  Adder #(.width(16)) adder_1 (.a(register_1_q), .b(16'h1), .out(adder_1_out));  // open: cin, cout
  ROM #(.addrWidth(16), .dataWidth(16)) rom_1 (.addr(register_1_q), .data({Opcode, RS, RT, RD_IMM}));  // open: sel
  Multiplexer #(.width(4), .enable("false")) multiplexer_1 (
    .in0(RD_IMM), .in1(RT), .out(multiplexer_1_out), .sel(in_4));
  assign bit_extender_1_out = {{12{1'b0}}, RD_IMM};  // Bit_Extender bit_extender_1
  Register_File_LAB_5 register_file_lab_5_1 (
    .Write(multiplexer_3_out), .Clock(button_1_out), .Read_1(register_file_lab_5_1_read_1),
    .Read_2(register_file_lab_5_1_read_2), .RD(multiplexer_1_out), .Wr_enable(in_6), .RS(RS), .RT(RT));
  Button button_1 (.out(button_1_out));
  Multiplexer #(.width(16), .enable("false")) multiplexer_2 (
    .in0(register_file_lab_5_1_read_2), .in1(bit_extender_1_out), .out(multiplexer_2_out), .sel(in_5));
  _16_bit_ALU_LAB_5 u_16_bit_alu_lab_5_1 (
    .A(register_file_lab_5_1_read_1), .A_2(multiplexer_2_out), .Binvert(Binvert), .Cin(Cin),
    .Operation(Operation), .Cout(out_15), .Result(out_14));
  Multiplexer #(.width(16), .enable("false")) multiplexer_3 (
    .in0(ram_1_data), .in1(out_14), .out(multiplexer_3_out), .sel(in_9));
  RAM #(.addrWidth(16), .dataWidth(16), .bus("separate")) ram_1 (
    .addr(out_14), .din(register_file_lab_5_1_read_2), .data(ram_1_data), .str(store), .clk(button_1_out),
    .ld(load));  // open: sel, clr

  // Notes on the sheet:
  //   contents of rom_1 (hex, n*v repeats v):
  //   123 456 762 983
endmodule

module Lab_8_Single_cycle_with_control (
  output [3:0] Opcode,
  output [3:0] RS,
  output [3:0] RT,
  output [3:0] RD_IMM,
  output [15:0] out_5,
  output out_6
);

  wire button_1_out, main_control_l8_1_alu_src, main_control_l8_1_load, main_control_l8_1_reg_dest,
       main_control_l8_1_result, main_control_l8_1_store, main_control_l8_1_sub, main_control_l8_1_write_en;
  wire [2:0] main_control_l8_1_aluop;
  wire [3:0] multiplexer_1_out;
  wire [15:0] adder_1_out, bit_extender_1_out, multiplexer_2_out, multiplexer_3_out, ram_1_data,
       register_1_q, register_file_lab_5_1_read_1, register_file_lab_5_1_read_2;

  Register #(.width(16)) register_1 (.D(adder_1_out), .Q(register_1_q), .clk(button_1_out));  // open: en, clr
  Adder #(.width(16)) adder_1 (.a(register_1_q), .b(16'h1), .out(adder_1_out));  // open: cin, cout
  ROM #(.addrWidth(16), .dataWidth(16)) rom_1 (.addr(register_1_q), .data({Opcode, RS, RT, RD_IMM}));  // open: sel
  Main_Control_L8 main_control_l8_1 (
    .opcode(Opcode), .Reg_dest(main_control_l8_1_reg_dest), .Write_En(main_control_l8_1_write_en),
    .ALu_Src(main_control_l8_1_alu_src), .ALUop(main_control_l8_1_aluop), .Sub(main_control_l8_1_sub),
    .Load(main_control_l8_1_load), .Store(main_control_l8_1_store), .Result(main_control_l8_1_result));
  Multiplexer #(.width(4), .enable("false")) multiplexer_1 (
    .in0(RD_IMM), .in1(RT), .out(multiplexer_1_out), .sel(main_control_l8_1_reg_dest));
  assign bit_extender_1_out = {{12{1'b0}}, RD_IMM};  // Bit_Extender bit_extender_1
  Register_File_LAB_5 register_file_lab_5_1 (
    .Write(multiplexer_3_out), .Clock(button_1_out), .Read_1(register_file_lab_5_1_read_1),
    .Read_2(register_file_lab_5_1_read_2), .RD(multiplexer_1_out), .Wr_enable(main_control_l8_1_write_en),
    .RS(RS), .RT(RT));
  Button button_1 (.out(button_1_out));
  Multiplexer #(.width(16), .enable("false")) multiplexer_2 (
    .in0(register_file_lab_5_1_read_2), .in1(bit_extender_1_out), .out(multiplexer_2_out),
    .sel(main_control_l8_1_alu_src));
  _16_bit_ALU_LAB_5 u_16_bit_alu_lab_5_1 (
    .A(register_file_lab_5_1_read_1), .A_2(multiplexer_2_out), .Binvert(main_control_l8_1_sub),
    .Cin(main_control_l8_1_sub), .Operation(main_control_l8_1_aluop), .Cout(out_6), .Result(out_5));
  Multiplexer #(.width(16), .enable("false")) multiplexer_3 (
    .in0(ram_1_data), .in1(out_5), .out(multiplexer_3_out), .sel(main_control_l8_1_result));
  RAM #(.addrWidth(16), .dataWidth(16), .bus("separate")) ram_1 (
    .addr(out_5), .din(register_file_lab_5_1_read_2), .data(ram_1_data), .str(main_control_l8_1_store),
    .clk(button_1_out), .ld(main_control_l8_1_load));  // open: sel, clr

  // Notes on the sheet:
  //   contents of rom_1 (hex, n*v repeats v):
  //   6125 6435 236 5661 7165
  //   Reg.Dest
  //   ALUsrc
  //   result mux
endmodule

module Main_Control_L8 (
  input  [3:0] opcode,
  output Reg_dest,
  output Write_En,
  output ALu_Src,
  output [2:0] ALUop,
  output Sub,
  output Load,
  output Store,
  output Result
);

  wire and_1_out, and_2_out, and_3_out, and_4_out, and_5_out, and_6_out, and_7_out, and_8_out, and_10_out,
       and_11_out, and_13_out, and_14_out, and_15_out, and_16_out, and_17_out, not_1_out, not_2_out,
       not_3_out, not_4_out, not_5_out, not_6_out, not_7_out, not_8_out, not_9_out, not_10_out, not_11_out,
       not_12_out, not_13_out, not_14_out, not_15_out, not_16_out, not_17_out, not_18_out, not_19_out,
       not_20_out, not_21_out, not_22_out, not_23_out, not_24_out, not_25_out, not_26_out, not_27_out,
       not_28_out, not_29_out, not_30_out, not_31_out, not_32_out, not_33_out, not_34_out, not_35_out,
       not_36_out;

  not not_1 (not_1_out, opcode[3]);
  and and_1 (and_1_out, not_1_out, opcode[2]);
  not not_2 (not_2_out, opcode[2]);
  and and_2 (and_2_out, opcode[3], not_2_out, not_3_out);
  not not_3 (not_3_out, opcode[1]);
  not not_4 (not_4_out, opcode[3]);
  and and_3 (and_3_out, not_4_out, not_5_out);
  not not_5 (not_5_out, opcode[2]);
  not not_6 (not_6_out, opcode[3]);
  and and_4 (and_4_out, not_6_out, not_7_out);
  not not_7 (not_7_out, opcode[1]);
  not not_8 (not_8_out, opcode[3]);
  and and_5 (and_5_out, not_8_out, not_9_out);
  not not_9 (not_9_out, opcode[0]);
  not not_10 (not_10_out, opcode[2]);
  and and_6 (and_6_out, not_10_out, not_11_out);
  not not_11 (not_11_out, opcode[1]);
  not not_12 (not_12_out, opcode[3]);
  and and_7 (and_7_out, not_12_out, opcode[2]);
  and and_8 (and_8_out, opcode[3], not_13_out, not_14_out);
  not not_13 (not_13_out, opcode[2]);
  not not_14 (not_14_out, opcode[1]);
  not not_15 (not_15_out, opcode[3]);
  and and_9 (ALUop[2], not_15_out, not_16_out, opcode[0]);
  not not_16 (not_16_out, opcode[1]);
  not not_17 (not_17_out, opcode[3]);
  and and_10 (and_10_out, not_17_out, not_18_out);
  not not_18 (not_18_out, opcode[1]);
  not not_19 (not_19_out, opcode[3]);
  and and_11 (and_11_out, not_19_out, opcode[2]);
  not not_20 (not_20_out, opcode[3]);
  not not_21 (not_21_out, opcode[2]);
  not not_22 (not_22_out, opcode[0]);
  not not_23 (not_23_out, opcode[2]);
  not not_24 (not_24_out, opcode[1]);
  not not_25 (not_25_out, opcode[0]);
  not not_26 (not_26_out, opcode[3]);
  not not_27 (not_27_out, opcode[1]);
  and and_12 (Sub, not_26_out, not_27_out, opcode[0]);
  not not_28 (not_28_out, opcode[3]);
  not not_29 (not_29_out, opcode[0]);
  not not_30 (not_30_out, opcode[3]);
  not not_31 (not_31_out, opcode[3]);
  and and_13 (and_13_out, not_31_out, not_32_out);
  not not_32 (not_32_out, opcode[2]);
  not not_33 (not_33_out, opcode[3]);
  and and_14 (and_14_out, not_33_out, not_34_out);
  not not_34 (not_34_out, opcode[1]);
  not not_35 (not_35_out, opcode[2]);
  and and_15 (and_15_out, not_35_out, not_36_out);
  not not_36 (not_36_out, opcode[1]);
  or or_1 (Reg_dest, and_1_out, and_2_out);
  or or_2 (Write_En, and_3_out, and_4_out, and_5_out, and_6_out);
  or or_3 (ALu_Src, and_7_out, and_8_out);
  or or_4 (ALUop[1], and_10_out, and_11_out);
  and and_16 (and_16_out, not_20_out, not_21_out, opcode[1], not_22_out);
  or or_5 (ALUop[0], and_16_out, and_17_out);
  and and_17 (and_17_out, opcode[3], not_23_out, not_24_out, not_25_out);
  and and_18 (Load, not_28_out, opcode[2], opcode[1], not_29_out);
  and and_19 (Store, not_30_out, opcode[2], opcode[1], opcode[0]);
  or or_6 (Result, and_13_out, and_14_out, and_15_out);
endmodule
